# Fritzing sketch design (saved by Fritzing 0.9.10b)
breadboards: 2

parts:
  Mod1 = Amica NodeMCU DEVKIT 1.0
  R1 = Resistor [tolerance=±5% resistance=10k package="2512 [SMD]"]
  R2 = Resistor [tolerance=±5% resistance=27k package="2512 [SMD]"]
  BAT1 = 12 battery [package=battery]
  A1 = DHT22 module

nets:
  N1: Mod1.pin1, Mod1.pin_10, Mod1.pin_26, A1.+
  N2: Mod1.pin2, Mod1.pin_9, Mod1.pin_25, Mod1.pin_29, R1.Pin_0, BAT1.-, A1.-
  N3: Mod1.pin_13, A1.Out
  N4: Mod1.pin_16, R1.Pin_1, R2.Pin_1
  N5: R2.Pin_0, BAT1.+

custom parts:
  12 battery: 12V lead acid type battery, like the Husqvarna YTH2448 12V 35AH battery. This is the mini version 1/4 the size of the actual battery to be closer to typical breadboard parts (around 2in wide rathher than 7in). The pads in pcb are sized to accomidate up to 14ga wire (as these batterys will deliver high currents.)
  DHT22 module: DHT22 module. Pins VCC Data GND.
